# Fritzing sketch ESPtank (saved by Fritzing 0.9.3b)
circuit board: 8.46667cm x 5.64444cm
breadboards: 2

parts:
  NodeMCU_v1 = NodeMCU v3 LoLin [part_number=ESP8266]
  R1 = Resistor [tolerance=±5% resistance=100k package=THT]
  NTC_100K = Temperature Sensor (Thermistor) [thermistor_type=NTC package=THT]
  Q1 = TRANSISTOR_NPN [part_number=n2222 package=to-92-ammo]
  F1 = Fan - Ventilador [package=THT]
  C1 = Electrolytic Capacitor [capacitance=100µF voltage=16V package="200 mil [THT, electrolytic]"]
  V1 = DC Power [voltage=12V]

nets:
  N1: NodeMCU_v1.3V3, NTC_100K.pin_0
  N2: NodeMCU_v1.GND#6, NodeMCU_v1.GND#13, NodeMCU_v1.GND#16, NodeMCU_v1.GND#33, Q1.E, V1.V-
  N3: NodeMCU_v1.D8, Q1.B
  VIN: NodeMCU_v1.VIN, F1.5V, C1.+, V1.V+
  N4: NodeMCU_v1.GND#41, R1.Pin_1
  N5: NodeMCU_v1.A0, R1.Pin_0, NTC_100K.pin_1
  N6: Q1.C, F1.GND, C1.-

custom parts:
  NodeMCU v3 LoLin: NodeMCU v3 LoLin NodeMCU (http://www.nodemcu.com/) is an open source IoT platform. It includes firmware (https://nodemcu-build.com/) which runs on the ESP8266 Wi-Fi SoC from Espressif Systems, and hardware which is based on the ESP-12E module. The term "NodeMCU" by default refers to the firmware rather than the dev kits. The firmware uses the Lua scripting language. It is based on the eLua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
  Fan - Ventilador: Ventilador de 2 pines, se encuentra comunmente en computadoras de escritorio
